# Fritzing sketch Balancing_Robot_V03_ohne_BT (saved by Fritzing 1.0.0rc)
breadboards: 2

parts:
  Part1 = Arduino Nano (Rev3.0)
  Part2 = InvenSense MPU6050
  Pololu_A2 = Pololu A4988 [package=SO16]
  C1 = Electrolytic Capacitor [capacitance=0.1mF voltage=50V package="100 mil [THT, electrolytic]"]
  U1 = LIPO-2000mAh [package=lipo-2200]
  M1 = Stepper Motor - Bipolar
  Pololu_A3 = Pololu A4988 [package=SO16]
  M2 = Stepper Motor - Bipolar
  LED2 = LED - 3mm [color="Green (555nm)" current=0.030A package="3 mm [THT]"]
  R2 = Resistor [tolerance=±5% power=0.25W resistance=330 package=THT]
  R1 = Resistor [tolerance=±5% power=0.25W resistance=220 package=THT]
  LED1 = LED - 3mm [color="Red (633nm)" current=0.030A package="3 mm [THT]"]
  S1 = Round Pushbutton
  S2 = Taiway 100-SP-X-T1 SPDT Miniature Toggle Switch [part_number=100-SP-X-T1-0-0-B1-M1 package=THT]
  S3 = Round Pushbutton
  R3 = Resistor [tolerance=±5% power=0.25W resistance=10k package=THT]
  R4 = Resistor [tolerance=±5% power=0.25W resistance=10k package=THT]
  R5 = Rotary Potentiometer (Small) [maximum_resistance=100kΩ knob_status=50% power=0.5W package=THT]

nets:
  GND: Part1.GND, Part2.GND, Pololu_A2.GND#8, Pololu_A3.GND#8, LED2.cathode, LED1.cathode, S1.leg0, S3.leg0, R5.leg1
  N1: Part1.D3, Pololu_A2.DIR
  N2: Part1.D4, Pololu_A2.STEP
  N3: Part1.D6, Pololu_A3.DIR
  N4: Part1.D7, Pololu_A3.STEP
  N5: Part1.D9, S3.leg1, R4.Pin_0
  N6: Part1.D10, S1.leg1, R3.Pin_0
  N7: Part1.D11/MOSI, R2.Pin_1
  N8: Part1.D12/MISO, R1.Pin_1
  VDD: Part1.5V, Part2.VCC, Pololu_A2.MS2, Pololu_A2.VDD, Pololu_A3.MS2, Pololu_A3.VDD, R3.Pin_1, R4.Pin_1, R5.leg2
  N9: Part1.A5, Part2.SCL
  N10: Part1.A4, Part2.SDA
  N11: Part1.A0, R5.wiper
  N12: Pololu_A2.RESET, Pololu_A2.SLEEP
  N13: Pololu_A2.1B, M1.D
  N14: Pololu_A2.1A, M1.B
  N15: Pololu_A2.2A, M1.C
  N16: Pololu_A2.2B, M1.A
  N17: Pololu_A2.GND#14, C1.-, U1.-, Pololu_A3.GND#14
  N18: Pololu_A2.VMOT, C1.+, U1.+, Pololu_A3.VMOT, S2.COM, S2.L1
  N19: Pololu_A3.RESET, Pololu_A3.SLEEP
  N20: Pololu_A3.1B, M2.D
  N21: Pololu_A3.1A, M2.B
  N22: Pololu_A3.2A, M2.C
  N23: Pololu_A3.2B, M2.A
  N24: LED2.anode, R2.Pin_0
  N25: R1.Pin_0, LED1.anode

notes:
  Motor 2
  Motor 1
  AD0=HIGH -> I2C-Adress: 0x69
  2200mAh 40C 11.1V
  6A 125V Kippschalter
  GY521 / MPU6050
  A4988 Motor-Treiber
  NEMA17 0.48Nm 1.5A Schrittmotor
  100µF Kondensator
  10kΩ Potientiometer

custom parts:
  LIPO-2000mAh: 2000mAh Lipo-battery
